# Fritzing sketch DispenserCircuit (saved by Fritzing 0.9.3b)
breadboards: 2

parts:
  Raspberry_Pi_1 = Raspberry Pi 3 [part_number=RPI-3-V1.2]
  HC-SR04_Sensor_1 = HC-SR04 Ultrasonic Distance Sensor
  R2 = Resistor [tolerance=±5% resistance=1k package=THT]
  R3 = Resistor [tolerance=±5% resistance=1k package=THT]
  R4 = Resistor [tolerance=±5% resistance=1k package=THT]
  HC-SR04_Sensor_2 = HC-SR04 Ultrasonic Distance Sensor
  HC-SR04_Sensor_3 = HC-SR04 Ultrasonic Distance Sensor
  R5 = Resistor [tolerance=±5% resistance=1k package=THT]
  R6 = Resistor [tolerance=±5% resistance=1k package=THT]
  R7 = Resistor [tolerance=±5% resistance=1k package=THT]
  R8 = Resistor [tolerance=±5% resistance=1k package=THT]
  R9 = Resistor [tolerance=±5% resistance=1k package=THT]
  R10 = Resistor [tolerance=±5% resistance=1k package=THT]
  JACK1 = 2.1mm Barrel Jack with Terminal Block
  M1 = Stepper Motor - Bipolar  # not connected
  M2 = Stepper Motor - Bipolar  # not connected
  Pololu_A1 = Pololu A4988 [package=SO16]
  Pololu_A2 = Pololu A4988 [package=SO16]

nets:
  3V3: Raspberry_Pi_1.3v3, Raspberry_Pi_1.3V3
  VCC: HC-SR04_Sensor_1.VCC, HC-SR04_Sensor_3.VCC, Pololu_A1.VDD, Pololu_A2.VDD
  N1: HC-SR04_Sensor_1.ECHO, R2.Pin_1
  GND: HC-SR04_Sensor_1.GND, HC-SR04_Sensor_3.GND, R8.Pin_1, Pololu_A1.GND#8, Pololu_A2.GND#8
  N2: R2.Pin_0, R3.Pin_0
  N3: R3.Pin_1, R4.Pin_0
  N4: HC-SR04_Sensor_2.ECHO, R7.Pin_1
  N5: HC-SR04_Sensor_2.GND, R6.Pin_1, JACK1.NEG, Pololu_A1.GND#14, Pololu_A2.2B, Pololu_A2.GND#14
  N6: HC-SR04_Sensor_3.ECHO, R10.Pin_1
  N7: R5.Pin_0, R7.Pin_0
  N8: R5.Pin_1, R6.Pin_0
  N9: R8.Pin_0, R9.Pin_1
  N10: R9.Pin_0, R10.Pin_0
  N11: JACK1.POS, Pololu_A1.VMOT, Pololu_A2.VMOT
  N12: Pololu_A1.RESET, Pololu_A1.SLEEP
  N13: Pololu_A2.RESET, Pololu_A2.SLEEP
